# Fritzing sketch Arduino-Basic-Project-#4-Fritzing-File (saved by Fritzing 0.9.3b)
breadboards: 1

parts:
  Part1 = Arduino Uno (Rev3)
  R1 = Resistor [tolerance=±5% resistance=220 package=THT]
  R2 = Resistor [tolerance=±5% resistance=220 package=THT]
  R3 = Resistor [tolerance=±5% resistance=220 package=THT]
  LED6 = RGB LED (com. cathode, rgb) [package="5 mm [THT]"]

nets:
  N1: Part1.D8, R3.Pin_0
  N2: Part1.D9_PWM, R2.Pin_0
  N3: Part1.D11_PWM/MOSI, R1.Pin_0
  N4: R1.Pin_1, LED6.red_anode
  N5: R2.Pin_1, LED6.green_anode
  N6: R3.Pin_1, LED6.blue_anode

notes:
  Note: Here we have used Common Cathode type RGB LED.
