# Fritzing sketch Arduino-Basic-Project-#5-fritzinf-file (saved by Fritzing 0.9.3b)
breadboards: 1

parts:
  Part1 = Arduino Uno (Rev3)
  LED1 = LED - 5mm [color="Red (633nm)" package="5 mm [THT]"]
  R1 = Rotary Potentiometer (Small) [maximum_resistance=10kΩ package=THT]

nets:
  N1: Part1.A0, R1.wiper
  N2: Part1.D9_PWM, LED1.anode
  N3: Part1.GND, LED1.cathode, R1.leg1
  N4: Part1.5V, R1.leg2
