# Fritzing sketch Arduino-Basic-Project-#6-fritzing-file (saved by Fritzing 0.9.3b)
breadboards: 1

parts:
  LED1 = LED - 5mm [color="Green (555nm)" package="5 mm [THT]"]
  R1 = Resistor [tolerance=±5% resistance=220 package=THT]
  S1 = Pushbutton [package="[THT]"]
  Part1 = Arduino Uno (Rev3)

nets:
  N1: LED1.cathode, R1.Pin_1
  N2: LED1.anode, Part1.D11_PWM/MOSI
  N3: R1.Pin_0, S1.Pin_3, S1.Pin_4, Part1.D10_PWM/SS
  N4: S1.Pin_1, S1.Pin_2, Part1.5V
