# Fritzing sketch Arduino-Basic-Project-#7-fritzing-file (saved by Fritzing 0.9.3b)
breadboards: 1

parts:
  R1 = Rotary Potentiometer (Small) [maximum_resistance=1kΩ package=THT]
  LED1 = LED - 5mm [color="Red (633nm)" package="5 mm [THT]"]
  LED2 = LED - 5mm [color="Green (570nm)" package="5 mm [THT]"]
  Part1 = Arduino Uno (Rev3)
  J1 = Piezo Speaker

nets:
  N1: R1.leg1, Part1.5V
  N2: R1.wiper, Part1.A0
  N3: R1.leg2, LED1.cathode, LED2.cathode, Part1.GND, J1.pin1
  N4: LED1.anode, Part1.D7
  N5: LED2.anode, Part1.D6_PWM
  N6: Part1.D5_PWM, J1.pin2
